# Fritzing sketch Garden Controller (saved by Fritzing 0.9.10b)
breadboards: 1

parts:
  Componente1 = Arduino Uno (Rev3)
  Componente2 = Bluetooth HC-05 Macho
  LED2 = LED - 5mm [color="Green (570nm)" current=0.030 package="5 mm [THT]"]
  LED3 = LED - 5mm [color="Green (570nm)" current=0.030 package="5 mm [THT]"]
  LED4 = LED - 5mm [color="Green (570nm)" current=0.030 package="5 mm [THT]"]
  LED5 = LED - 5mm [color="Green (570nm)" current=0.030 package="5 mm [THT]"]
  R1 = Resistor [tolerance=±5% power=0.25 resistance=220 package=THT]
  R2 = Resistor [tolerance=±5% power=0.25 resistance=220 package=THT]
  R3 = Resistor [tolerance=±5% power=0.25 resistance=220 package=THT]
  R4 = Resistor [tolerance=±5% power=0.25 resistance=220 package=THT]
  R5 = Resistor [tolerance=±5% power=0.25 resistance=1k package=THT]
  R6 = Resistor [tolerance=±5% power=0.25 resistance=2.2k package=THT]
  J1 = Basic Servo

nets:
  N1: Componente1.D8, LED3.cathode, R1.Pin_0
  N2: Componente1.D10_PWM/SS, R5.Pin_1
  N3: Componente1.D11_PWM/MOSI, Componente2.TXD
  N4: Componente1.D13/SCK, Componente2.State
  N5: Componente1.D2, LED2.anode
  N6: Componente1.D3_PWM, J1.pulse
  N7: Componente1.D5_PWM, LED4.anode
  N8: Componente1.D6_PWM, LED5.anode
  VCC: Componente1.5V, Componente2.VCC, J1.vcc
  GND: Componente1.GND, Componente2.GND, R1.Pin_1, R2.Pin_1, R3.Pin_1, R4.Pin_1, R6.Pin_1, J1.gnd
  N9: Componente2.RXD, R5.Pin_0, R6.Pin_0
  N10: LED2.cathode, R3.Pin_0
  N11: LED4.cathode, R2.Pin_0
  N12: LED5.cathode, R4.Pin_0
