# Fritzing sketch Garden Sensorboard (saved by Fritzing 0.9.10b)
breadboards: 1

parts:
  Mod1 = Heltec WiFi LoRa 32 V2 [part_number=HTIT-WB32LA]
  R1 = PHOTOCELL [package=photocell]
  DHT1 = Humidity and Temperature Sensor DHT11
  R2 = Resistor [tolerance=±5% resistance=220 package="2512 [SMD]"]
  R3 = Resistor [tolerance=±5% resistance=10k package="2512 [SMD]"]
  LED1 = LED - 5mm [color="Green (570nm)" current=0.030 package="5 mm [THT]"]

nets:
  N1: Mod1.pin_4, DHT1.Data-signal
  N2: Mod1.pin_5, LED1.anode
  N3: Mod1.pin_16, Mod1.pin_17, R1.P$2, DHT1.Vcc
  N4: Mod1.GND, DHT1.GND_2, R2.Pin_1, R3.Pin_0
  N5: Mod1.pin_35, R1.P$1, R3.Pin_1
  N6: R2.Pin_0, LED1.cathode

notes:
  Ho utilizzato un sensore DHT11 a tre pin con la resistenza integrata, per questo non è presente
  Ho Utilizzato un esp32 leggermente diverso da quello del laboratorio, i pin potrebbero essere leggermente diversi

custom parts:
  Humidity and Temperature Sensor DHT11: Digital relative humidity & temperature sensor DHT11
